# Fritzing sketch Gymproto1 (saved by Fritzing 0.9.3b)

parts:
  SEN1 = Pulse_Sensor
  부품3 = Bluetooth HC-05 Macho
  o1 = Module display OLED I2C 128x64 SSD1306 [package=THT]
  부품2 = Arduino Uno (Rev3)

nets:
  N1: SEN1.connector2, 부품2.A0
  N2: 부품3.TXD, 부품2.D2
  N3: 부품3.RXD, 부품2.D3_PWM
  GND: o1.GND, 부품2.GND
  VCC: o1.VCC, 부품2.5V
  N4: o1.SCL, 부품2.A5/SCL
  N5: o1.SDA, 부품2.A4/SDA

custom parts:
  Module display OLED I2C 128x64 SSD1306: Ecran OLED I2C SSD163 de 128x64 avec connexion I2C
